# Fritzing sketch _3D_LED_7_Segment_circuit (saved by Fritzing 0.9.3b)
breadboards: 1

parts:
  Part1 = Arduino Nano (Rev3.0)
  DS1 = DS18B20 1-Wire Temperature Sensor [part_number=DS18B20]
  R1 = Resistor [tolerance=±5% resistance=4.7k package="0603 [SMD]"]
  LED_full_1903 = Header 3 [package=molex-1x3_lock]

nets:
  GND: Part1.GND, DS1.GND, LED_full_1903.1
  N1: Part1.D2, DS1.DQ, R1.Pin_1
  N2: Part1.D3, LED_full_1903.2
  N3: Part1.VIN, LED_full_1903.3
  5V: Part1.5V, DS1.VDD, R1.Pin_0
